# Fritzing sketch servo (saved by Fritzing 0.9.0b)
breadboards: 1

parts:
  Part1 = Spark Core (v1.0)
  VCC1 = 4 x AAA Battery Mount
  J1 = Basic Servo
  C3 = Electrolytic Capacitor [capacitance=1μF package="0405 [SMD, electrolytic]"]

nets:
  N1: Part1.A1, J1.pulse
  GND: Part1.GND, VCC1.-, J1.gnd, C3.-
  VIN: Part1.VIN, VCC1.+, J1.vcc, C3.+
